// Logisim project 同步复位.circ as structural Verilog: 8 circuits, main circuit main
module main (
  input  in_1,
  output [31:0] out_2,
  output out_3,
  output [4:0] out_4,
  output [31:0] out_5,
  output out_6,
  output [4:0] out_7,
  output [31:0] out_8
);

  wire ALUSrc, Clk, comparator_1_eq, MemtoReg, nPC_sel, nPC_sel2, RegDst;
  wire [1:0] ExtOp;
  wire [2:0] ALUctr;
  wire [31:0] ALUresult, ext_1_extimm, multiplexer_3_out, NPC, nPC1, nPC2, RD, RD1, shifter_1_out;

  Clock clock_1 (.out(Clk));
  Multiplexer #(.width(5)) multiplexer_1 (
    .in0(out_2[20:16]), .in1(out_2[15:11]), .out(out_4), .sel(RegDst));  // open: en
  Multiplexer #(.width(32)) multiplexer_2 (
    .in0({ALUresult[31:7], out_7, ALUresult[1:0]}), .in1(RD), .out(out_5), .sel(MemtoReg));  // open: en
  NPC npc_1 (.nPC1(nPC1), .nPC2(nPC2), .nPC(NPC), .nPC_sel2(nPC_sel2), .Reset(in_1), .clk(Clk));
  Comparator #(.width(32)) comparator_1 (
    .a({32{1'b0}}), .b({ALUresult[31:7], out_7, ALUresult[1:0]}), .eq(comparator_1_eq));  // open: gt, lt
  IM IM (.A(NPC[6:2]), .RD(out_2));
  Adder #(.width(32)) adder_1 (.a(NPC), .b(32'h4), .out(nPC1));  // open: cin, cout
  GRF GRF (
    .A1(out_2[25:21]), .A2(out_2[20:16]), .A3(out_4), .WD3(out_5), .RD1(RD1), .RD2(out_8), .in_1(Clk),
    .in_2(out_3), .in_6(in_1));
  and and_1 (nPC_sel2, comparator_1_eq, nPC_sel);
  ALU alu_1 (
    .in_1(RD1), .in_2(multiplexer_3_out), .ALUresult({ALUresult[31:7], out_7, ALUresult[1:0]}),
    .ALUctr(ALUctr));
  EXT ext_1 (.IMM(out_2[15:0]), .ExtIMM(ext_1_extimm), .ExtOp(ExtOp));
  // Probe on RD1
  Multiplexer #(.width(32)) multiplexer_3 (
    .in0(out_8), .in1(ext_1_extimm), .out(multiplexer_3_out), .sel(ALUSrc));  // open: en
  Shifter #(.width(32)) shifter_1 (.in(ext_1_extimm), .\dist (5'b00010), .out(shifter_1_out));
  Adder #(.width(32)) adder_2 (.a(shifter_1_out), .b(nPC1), .out(nPC2));  // open: cin, cout
  Control_Unit control_unit_1 (
    .opcode(out_2[31:26]), .RegDst(RegDst), .ALUSrc(ALUSrc), .MemtoReg(MemtoReg), .RegWrite(out_3),
    .MemWrite(out_6), .nPC_sel(nPC_sel), .ALUctr(ALUctr), .ExtOp(ExtOp), .funct(out_2[5:0]));
  DM dm_1 (.A(out_7), .WD(out_8), .RD(RD), .WE(out_6), .Clk(Clk));

  // Other names for the same wires on the sheet: A1[4:0] = out_2[25:21]; Instr[31:0] = out_2; A2[4:0] = out_2[20:16];
  //   ALUresult[6:2] = out_7; MemAddr[4:0] = out_7; funct[5:0] = out_2[5:0]; IMM[15:0] = out_2[15:0];
  //   shamt[4:0] = out_2[10:6]; A3[4:0] = out_2[15:11]; MemWrite = out_6; opcode[5:0] = out_2[31:26];
  //   MemData[31:0] = out_8; RD2[31:0] = out_8; RegAddr[4:0] = out_4; RegData[31:0] = out_5; RegWrite = out_3;
  //   Reset = in_1

  // Notes on the sheet:
  //   pc
  //   Instr
endmodule

module IM (
  input  [4:0] A,
  output [31:0] RD
);

  ROM #(.addrWidth(5), .dataWidth(32)) rom_1 (.addr(A), .data(RD));  // open: sel

  // Notes on the sheet:
  //   contents of rom_1 (hex, n*v repeats v):
  //   34010001 224021 34201111 0 34091000 35290111 1295021 12a5823 3c090001 d4821 11200001 8c0a0000
  //   ac0a0000
endmodule

module GRF (
  input  in_1,
  input  in_2,
  input  [4:0] A1,
  input  [4:0] A2,
  input  [4:0] A3,
  input  in_6,
  input  [31:0] WD3,
  output [31:0] RD1,
  output [31:0] RD2
);

  wire decoder_1_out0, S1, S2, S3, S4, S5, S6, S7, S8, S9, S10, S11, S12, S13, S14, S15, S16, S17, S18, S19,
       S20, S21, S22, S23, S24, S25, S26, S27, S28, S29, S30, S31, undriven, WE3;
  wire [31:0] _0, _1, _2, _3, _4, _5, _6, _7, _8, _9, _10, _11, _12, _13, _14, _15, _16, _17, _18, _19, _20,
       _21, _22, _23, _24, _25, _26, _27, _28, _29, _30, _31, N1, n1_t, N2, n2_t, N3, n3_t, N4, n4_t, N5,
       n5_t, N6, n6_t, N7, n7_t, N8, n8_t, N9, n9_t, N10, n10_t, N11, n11_t, N12, n12_t, N13, n13_t, N14,
       n14_t, N15, n15_t, N16, n16_t, N17, n17_t, N18, n18_t, N19, n19_t, N20, n20_t, N21, n21_t, N22, n22_t,
       N23, n23_t, N24, n24_t, N25, n25_t, N26, n26_t, N27, n27_t, N28, n28_t, N29, n29_t, N30, n30_t, N31,
       n31_t;

  Register #(.width(32)) register_1 (.Q(_0));  // open: D, en, clk, clr
  Register #(.width(32)) register_2 (.D(N1), .en(WE3), .Q(_1), .clk(in_1));  // open: clr
  Register #(.width(32)) register_3 (.D(N2), .en(WE3), .Q(_2), .clk(in_1));  // open: clr
  Register #(.width(32)) register_4 (.D(N3), .en(WE3), .Q(_3), .clk(in_1));  // open: clr
  Register #(.width(32)) register_5 (.D(N4), .en(WE3), .Q(_4), .clk(in_1));  // open: clr
  Register #(.width(32)) register_6 (.D(N5), .en(WE3), .Q(_5), .clk(in_1));  // open: clr
  Register #(.width(32)) register_7 (.D(N6), .en(WE3), .Q(_6), .clk(in_1));  // open: clr
  Register #(.width(32)) register_8 (.D(N7), .en(WE3), .Q(_7), .clk(in_1));  // open: clr
  Multiplexer #(.width(32)) multiplexer_1 (.in0(_1), .in1(WD3), .out(n1_t), .sel(S1));  // open: en
  Multiplexer #(.width(32)) multiplexer_2 (.in0(_2), .in1(WD3), .out(n2_t), .sel(S2));  // open: en
  Multiplexer #(.width(32)) multiplexer_3 (.in0(_3), .in1(WD3), .out(n3_t), .sel(S3));  // open: en
  Multiplexer #(.width(32)) multiplexer_4 (.in0(_4), .in1(WD3), .out(n4_t), .sel(S4));  // open: en
  Multiplexer #(.width(32)) multiplexer_5 (.in0(_17), .in1(WD3), .out(n17_t), .sel(S17));  // open: en
  Multiplexer #(.width(32)) multiplexer_6 (.in0(_18), .in1(WD3), .out(n18_t), .sel(S18));  // open: en
  Multiplexer #(.width(32)) multiplexer_7 (.in0(_19), .in1(WD3), .out(n19_t), .sel(S19));  // open: en
  Multiplexer #(.width(32)) multiplexer_8 (.in0(_20), .in1(WD3), .out(n20_t), .sel(S20));  // open: en
  Register #(.width(32)) register_9 (.D(N8), .en(WE3), .Q(_8), .clk(in_1));  // open: clr
  Register #(.width(32)) register_10 (.D(N9), .en(WE3), .Q(_9), .clk(in_1));  // open: clr
  Register #(.width(32)) register_11 (.D(N10), .en(WE3), .Q(_10), .clk(in_1));  // open: clr
  Register #(.width(32)) register_12 (.D(N11), .en(WE3), .Q(_11), .clk(in_1));  // open: clr
  Register #(.width(32)) register_13 (.D(N12), .en(WE3), .Q(_12), .clk(in_1));  // open: clr
  Register #(.width(32)) register_14 (.D(N13), .en(WE3), .Q(_13), .clk(in_1));  // open: clr
  Register #(.width(32)) register_15 (.D(N14), .en(WE3), .Q(_14), .clk(in_1));  // open: clr
  Register #(.width(32)) register_16 (.D(N15), .en(WE3), .Q(_15), .clk(in_1));  // open: clr
  Multiplexer #(.width(32)) multiplexer_9 (.in0(_5), .in1(WD3), .out(n5_t), .sel(S5));  // open: en
  Multiplexer #(.width(32)) multiplexer_10 (.in0(_6), .in1(WD3), .out(n6_t), .sel(S6));  // open: en
  Multiplexer #(.width(32)) multiplexer_11 (.in0(_7), .in1(WD3), .out(n7_t), .sel(S7));  // open: en
  Multiplexer #(.width(32)) multiplexer_12 (.in0(_8), .in1(WD3), .out(n8_t), .sel(S8));  // open: en
  Multiplexer #(.width(32)) multiplexer_13 (.in0(_21), .in1(WD3), .out(n21_t), .sel(S21));  // open: en
  Multiplexer #(.width(32)) multiplexer_14 (.in0(_22), .in1(WD3), .out(n22_t), .sel(S22));  // open: en
  Multiplexer #(.width(32)) multiplexer_15 (.in0(_23), .in1(WD3), .out(n23_t), .sel(S23));  // open: en
  Multiplexer #(.width(32)) multiplexer_16 (.in0(_24), .in1(WD3), .out(n24_t), .sel(S24));  // open: en
  Register #(.width(32)) register_17 (.D(N16), .en(WE3), .Q(_16), .clk(in_1));  // open: clr
  Register #(.width(32)) register_18 (.D(N17), .en(WE3), .Q(_17), .clk(in_1));  // open: clr
  Register #(.width(32)) register_19 (.D(N18), .en(WE3), .Q(_18), .clk(in_1));  // open: clr
  Register #(.width(32)) register_20 (.D(N19), .en(WE3), .Q(_19), .clk(in_1));  // open: clr
  Register #(.width(32)) register_21 (.D(N20), .en(WE3), .Q(_20), .clk(in_1));  // open: clr
  Register #(.width(32)) register_22 (.D(N21), .en(WE3), .Q(_21), .clk(in_1));  // open: clr
  Register #(.width(32)) register_23 (.D(N22), .en(WE3), .Q(_22), .clk(in_1));  // open: clr
  Register #(.width(32)) register_24 (.D(N23), .en(WE3), .Q(_23), .clk(in_1));  // open: clr
  Multiplexer #(.width(32)) multiplexer_17 (.in0(_9), .in1(WD3), .out(n9_t), .sel(S9));  // open: en
  Multiplexer #(.width(32)) multiplexer_18 (.in0(_10), .in1(WD3), .out(n10_t), .sel(S10));  // open: en
  Multiplexer #(.width(32)) multiplexer_19 (.in0(_11), .in1(WD3), .out(n11_t), .sel(S11));  // open: en
  Multiplexer #(.width(32)) multiplexer_20 (.in0(_12), .in1(WD3), .out(n12_t), .sel(S12));  // open: en
  Multiplexer #(.width(32)) multiplexer_21 (.in0(_25), .in1(WD3), .out(n25_t), .sel(S25));  // open: en
  Multiplexer #(.width(32)) multiplexer_22 (.in0(_26), .in1(WD3), .out(n26_t), .sel(S26));  // open: en
  Multiplexer #(.width(32)) multiplexer_23 (.in0(_27), .in1(WD3), .out(n27_t), .sel(S27));  // open: en
  Multiplexer #(.width(32)) multiplexer_24 (.in0(_28), .in1(WD3), .out(n28_t), .sel(S28));  // open: en
  Register #(.width(32)) register_25 (.D(N24), .en(WE3), .Q(_24), .clk(in_1));  // open: clr
  Register #(.width(32)) register_26 (.D(N25), .en(WE3), .Q(_25), .clk(in_1));  // open: clr
  Register #(.width(32)) register_27 (.D(N26), .en(WE3), .Q(_26), .clk(in_1));  // open: clr
  Register #(.width(32)) register_28 (.D(N27), .en(WE3), .Q(_27), .clk(in_1));  // open: clr
  Register #(.width(32)) register_29 (.D(N28), .en(WE3), .Q(_28), .clk(in_1));  // open: clr
  Register #(.width(32)) register_30 (.D(N29), .en(WE3), .Q(_29), .clk(in_1));  // open: clr
  Register #(.width(32)) register_31 (.D(N30), .en(WE3), .Q(_30), .clk(in_1));  // open: clr
  Register #(.width(32)) register_32 (.D(N31), .en(WE3), .Q(_31), .clk(in_1));  // open: clr
  Multiplexer #(.width(32)) multiplexer_25 (.in0(_13), .in1(WD3), .out(n13_t), .sel(S13));  // open: en
  Multiplexer #(.width(32)) multiplexer_26 (.in0(_14), .in1(WD3), .out(n14_t), .sel(S14));  // open: en
  Multiplexer #(.width(32)) multiplexer_27 (.in0(_15), .in1(WD3), .out(n15_t), .sel(S15));  // open: en
  Multiplexer #(.width(32)) multiplexer_28 (.in0(_16), .in1(WD3), .out(n16_t), .sel(S16));  // open: en
  Multiplexer #(.width(32)) multiplexer_29 (.in0(_29), .in1(WD3), .out(n29_t), .sel(S29));  // open: en
  Multiplexer #(.width(32)) multiplexer_30 (.in0(_30), .in1(WD3), .out(n30_t), .sel(S30));  // open: en
  Multiplexer #(.width(32)) multiplexer_31 (.in0(_31), .in1(WD3), .out(n31_t), .sel(S31));  // open: en
  Decoder #(.select(5)) decoder_1 (
    .out0(decoder_1_out0), .out1(S1), .out2(S2), .out3(S3), .out4(S4), .out5(S5), .out6(S6), .out7(S7),
    .out8(S8), .out9(S9), .out10(S10), .out11(S11), .out12(S12), .out13(S13), .out14(S14), .out15(S15),
    .out16(S16), .out17(S17), .out18(S18), .out19(S19), .out20(S20), .out21(S21), .out22(S22), .out23(S23),
    .out24(S24), .out25(S25), .out26(S26), .out27(S27), .out28(S28), .out29(S29), .out30(S30), .out31(S31),
    .sel(A3));  // open: en
  Multiplexer #(.select(5), .width(32)) multiplexer_32 (
    .in0(_0), .in1(_1), .in2(_2), .in3(_3), .in4(_4), .in5(_5), .in6(_6), .in7(_7), .in8(_8), .in9(_9),
    .in10(_10), .in11(_11), .in12(_12), .in13(_13), .in14(_14), .in15(_15), .in16(_16), .in17(_17),
    .in18(_18), .in19(_19), .in20(_20), .in21(_21), .in22(_22), .in23(_23), .in24(_24), .in25(_25),
    .in26(_26), .in27(_27), .in28(_28), .in29(_29), .in30(_30), .in31(_31), .out(RD1), .sel(A1), .en(undriven));
  Multiplexer #(.width(32)) multiplexer_33 (.in0(n1_t), .in1({32{1'b0}}), .out(N1), .sel(in_6));  // open: en
  Multiplexer #(.width(32)) multiplexer_34 (.in0(n2_t), .in1({32{1'b0}}), .out(N2), .sel(in_6));  // open: en
  Multiplexer #(.width(32)) multiplexer_35 (.in0(n3_t), .in1({32{1'b0}}), .out(N3), .sel(in_6));  // open: en
  Multiplexer #(.width(32)) multiplexer_36 (.in0(n4_t), .in1({32{1'b0}}), .out(N4), .sel(in_6));  // open: en
  Multiplexer #(.width(32)) multiplexer_37 (.in0(n17_t), .in1({32{1'b0}}), .out(N17), .sel(in_6));  // open: en
  Multiplexer #(.width(32)) multiplexer_38 (.in0(n18_t), .in1({32{1'b0}}), .out(N18), .sel(in_6));  // open: en
  Multiplexer #(.width(32)) multiplexer_39 (.in0(n19_t), .in1({32{1'b0}}), .out(N19), .sel(in_6));  // open: en
  Multiplexer #(.width(32)) multiplexer_40 (.in0(n20_t), .in1({32{1'b0}}), .out(N20), .sel(in_6));  // open: en
  Multiplexer #(.select(5), .width(32)) multiplexer_41 (
    .in0(_0), .in1(_1), .in2(_2), .in3(_3), .in4(_4), .in5(_5), .in6(_6), .in7(_7), .in8(_8), .in9(_9),
    .in10(_10), .in11(_11), .in12(_12), .in13(_13), .in14(_14), .in15(_15), .in16(_16), .in17(_17),
    .in18(_18), .in19(_19), .in20(_20), .in21(_21), .in22(_22), .in23(_23), .in24(_24), .in25(_25),
    .in26(_26), .in27(_27), .in28(_28), .in29(_29), .in30(_30), .in31(_31), .out(RD2), .sel(A2));  // open: en
  or or_1 (WE3, in_2, in_6);
  Multiplexer #(.width(32)) multiplexer_42 (.in0(n5_t), .in1({32{1'b0}}), .out(N5), .sel(in_6));  // open: en
  Multiplexer #(.width(32)) multiplexer_43 (.in0(n6_t), .in1({32{1'b0}}), .out(N6), .sel(in_6));  // open: en
  Multiplexer #(.width(32)) multiplexer_44 (.in0(n7_t), .in1({32{1'b0}}), .out(N7), .sel(in_6));  // open: en
  Multiplexer #(.width(32)) multiplexer_45 (.in0(n8_t), .in1({32{1'b0}}), .out(N8), .sel(in_6));  // open: en
  Multiplexer #(.width(32)) multiplexer_46 (.in0(n21_t), .in1({32{1'b0}}), .out(N21), .sel(in_6));  // open: en
  Multiplexer #(.width(32)) multiplexer_47 (.in0(n22_t), .in1({32{1'b0}}), .out(N22), .sel(in_6));  // open: en
  Multiplexer #(.width(32)) multiplexer_48 (.in0(n23_t), .in1({32{1'b0}}), .out(N23), .sel(in_6));  // open: en
  Multiplexer #(.width(32)) multiplexer_49 (.in0(n24_t), .in1({32{1'b0}}), .out(N24), .sel(in_6));  // open: en
  Multiplexer #(.width(32)) multiplexer_50 (.in0(n9_t), .in1({32{1'b0}}), .out(N9), .sel(in_6));  // open: en
  Multiplexer #(.width(32)) multiplexer_51 (.in0(n10_t), .in1({32{1'b0}}), .out(N10), .sel(in_6));  // open: en
  Multiplexer #(.width(32)) multiplexer_52 (.in0(n11_t), .in1({32{1'b0}}), .out(N11), .sel(in_6));  // open: en
  Multiplexer #(.width(32)) multiplexer_53 (.in0(n12_t), .in1({32{1'b0}}), .out(N12), .sel(in_6));  // open: en
  Multiplexer #(.width(32)) multiplexer_54 (.in0(n25_t), .in1({32{1'b0}}), .out(N25), .sel(in_6));  // open: en
  Multiplexer #(.width(32)) multiplexer_55 (.in0(n26_t), .in1({32{1'b0}}), .out(N26), .sel(in_6));  // open: en
  Multiplexer #(.width(32)) multiplexer_56 (.in0(n27_t), .in1({32{1'b0}}), .out(N27), .sel(in_6));  // open: en
  Multiplexer #(.width(32)) multiplexer_57 (.in0(n28_t), .in1({32{1'b0}}), .out(N28), .sel(in_6));  // open: en
  Multiplexer #(.width(32)) multiplexer_58 (.in0(n13_t), .in1({32{1'b0}}), .out(N13), .sel(in_6));  // open: en
  Multiplexer #(.width(32)) multiplexer_59 (.in0(n14_t), .in1({32{1'b0}}), .out(N14), .sel(in_6));  // open: en
  Multiplexer #(.width(32)) multiplexer_60 (.in0(n15_t), .in1({32{1'b0}}), .out(N15), .sel(in_6));  // open: en
  Multiplexer #(.width(32)) multiplexer_61 (.in0(n16_t), .in1({32{1'b0}}), .out(N16), .sel(in_6));  // open: en
  Multiplexer #(.width(32)) multiplexer_62 (.in0(n29_t), .in1({32{1'b0}}), .out(N29), .sel(in_6));  // open: en
  Multiplexer #(.width(32)) multiplexer_63 (.in0(n30_t), .in1({32{1'b0}}), .out(N30), .sel(in_6));  // open: en
  Multiplexer #(.width(32)) multiplexer_64 (.in0(n31_t), .in1({32{1'b0}}), .out(N31), .sel(in_6));  // open: en

  // Other names for the same wires on the sheet: Clk = in_1; Reset = in_6; WE = in_2
endmodule

module Control_Unit (
  input  [5:0] opcode,
  input  [5:0] funct,
  output RegDst,
  output ALUSrc,
  output MemtoReg,
  output RegWrite,
  output MemWrite,
  output nPC_sel,
  output [2:0] ALUctr,
  output [1:0] ExtOp
);

  wire addu, and_1_out, and_7_out, and_8_out, beq, lui, lw, not_1_out, not_2_out, not_3_out, not_4_out,
       not_5_out, not_6_out, not_7_out, not_8_out, not_9_out, not_10_out, not_11_out, not_12_out, ori, subu,
       sw;
  wire [1:0] adder_1_out, adder_2_out, multiplexer_1_out, multiplexer_2_out, multiplexer_3_out,
       multiplexer_4_out;
  wire [3:0] adder_4_out, adder_5_out, adder_6_out, adder_7_out, adder_8_out, ALU, multiplexer_5_out,
       multiplexer_6_out, multiplexer_7_out, multiplexer_8_out, multiplexer_10_out, multiplexer_11_out,
       multiplexer_12_out;

  not not_1 (not_1_out, opcode[0]);
  not not_2 (not_2_out, opcode[1]);
  not not_3 (not_3_out, opcode[3]);
  not not_4 (not_4_out, opcode[2]);
  not not_5 (not_5_out, opcode[4]);
  not not_6 (not_6_out, opcode[5]);
  and and_1 (and_1_out, not_6_out, not_5_out, not_3_out, not_4_out, not_2_out, not_1_out);
  and and_2 (ori, not_6_out, not_5_out, opcode[3], opcode[2], not_2_out, opcode[0]);
  and and_3 (lw, opcode[5], not_5_out, not_3_out, not_4_out, opcode[1], opcode[0]);
  and and_4 (sw, opcode[5], not_5_out, opcode[3], not_4_out, opcode[1], opcode[0]);
  and and_5 (beq, not_6_out, not_5_out, not_3_out, opcode[2], not_2_out, not_1_out);
  and and_6 (lui, not_6_out, not_5_out, opcode[3], opcode[2], opcode[1], opcode[0]);
  and and_7 (and_7_out, funct[5], not_8_out, not_9_out, not_10_out, not_11_out, funct[0]);
  and and_8 (and_8_out, funct[5], not_8_out, not_9_out, not_10_out, funct[1], funct[0]);
  and and_9 (addu, and_1_out, and_7_out);
  and and_10 (subu, and_8_out, and_1_out);
  not not_7 (not_7_out, funct[5]);
  not not_8 (not_8_out, funct[4]);
  not not_9 (not_9_out, funct[3]);
  Multiplexer #(.width(2)) multiplexer_1 (.in0(2'b00), .in1(2'b01), .out(multiplexer_1_out), .sel(lw));  // open: en
  Multiplexer #(.width(2)) multiplexer_2 (.in0(2'b00), .in1(2'b10), .out(multiplexer_2_out), .sel(lui));  // open: en
  not not_10 (not_10_out, funct[2]);
  not not_11 (not_11_out, funct[1]);
  Adder #(.width(2)) adder_1 (.a(multiplexer_1_out), .b(multiplexer_2_out), .out(adder_1_out));  // open: cin, cout
  not not_12 (not_12_out, funct[0]);
  or or_1 (RegDst, addu, subu);
  or or_2 (ALUSrc, ori, sw, lui, lw);
  buf or_3 (MemtoReg, lw);  // OR_Gate
  or or_4 (RegWrite, ori, subu, addu, lui, lw);
  buf or_5 (MemWrite, sw);  // OR_Gate
  buf or_6 (nPC_sel, beq);  // OR_Gate
  Adder #(.width(2)) adder_2 (.a(adder_1_out), .b(multiplexer_3_out), .out(adder_2_out));  // open: cin, cout
  Multiplexer #(.width(2)) multiplexer_3 (.in0(2'b00), .in1(2'b01), .out(multiplexer_3_out), .sel(sw));  // open: en
  Multiplexer #(.width(2)) multiplexer_4 (.in0(2'b00), .in1(2'b01), .out(multiplexer_4_out), .sel(beq));  // open: en
  Adder #(.width(2)) adder_3 (.a(adder_2_out), .b(multiplexer_4_out), .out(ExtOp));  // open: cin, cout
  Multiplexer #(.width(4)) multiplexer_5 (
    .in0(4'b0000), .in1(4'b0001), .out(multiplexer_5_out), .sel(addu));  // open: en
  Multiplexer #(.width(4)) multiplexer_6 (
    .in0(4'b0000), .in1(4'b0010), .out(multiplexer_6_out), .sel(subu));  // open: en
  Adder #(.width(4)) adder_4 (.a(multiplexer_5_out), .b(multiplexer_6_out), .out(adder_4_out));  // open: cin, cout
  Multiplexer #(.width(4)) multiplexer_7 (.in0(4'b0000), .in1(4'b0001), .out(multiplexer_7_out), .sel(sw));  // open: en
  Adder #(.width(4)) adder_5 (.a(adder_4_out), .b(multiplexer_7_out), .out(adder_5_out));  // open: cin, cout
  Multiplexer #(.width(4)) multiplexer_8 (.in0(4'b0000), .in1(4'b0001), .out(multiplexer_8_out), .sel(lw));  // open: en
  Multiplexer #(.select(4), .width(3)) multiplexer_9 (
    .in0(3'b000), .in1(3'b001), .in2(3'b010), .in3(3'b011), .in4(3'b100), .out(ALUctr), .sel(ALU));  // open: in5, in6, in7, in8, in9, in10, in11, in12, in13, in14, in15, en
  Adder #(.width(4)) adder_6 (.a(adder_5_out), .b(multiplexer_8_out), .out(adder_6_out));  // open: cin, cout
  Multiplexer #(.width(4)) multiplexer_10 (
    .in0(4'b0000), .in1(4'b0010), .out(multiplexer_10_out), .sel(beq));  // open: en
  Adder #(.width(4)) adder_7 (.a(adder_6_out), .b(multiplexer_10_out), .out(adder_7_out));  // open: cin, cout
  Multiplexer #(.width(4)) multiplexer_11 (
    .in0(4'b0000), .in1(4'b0011), .out(multiplexer_11_out), .sel(ori));  // open: en
  Adder #(.width(4)) adder_8 (.a(adder_7_out), .b(multiplexer_11_out), .out(adder_8_out));  // open: cin, cout
  Multiplexer #(.width(4)) multiplexer_12 (
    .in0(4'b0000), .in1(4'b0100), .out(multiplexer_12_out), .sel(lui));  // open: en
  Adder #(.width(4)) adder_9 (.a(adder_8_out), .b(multiplexer_12_out), .out(ALU));  // open: cin, cout

  // Other names for the same wires on the sheet: fu0 = funct[0]; fu1 = funct[1]; fu2 = funct[2]; fu3 = funct[3];
  //   fu4 = funct[4]; fu5 = funct[5]; op0 = opcode[0]; op1 = opcode[1]; op2 = opcode[2]; op3 = opcode[3];
  //   op4 = opcode[4]; op5 = opcode[5]
endmodule

module EXT (
  input  [15:0] IMM,
  input  [1:0] ExtOp,
  output [31:0] ExtIMM
);

  wire [31:0] bit_extender_1_out, bit_extender_2_out;

  assign bit_extender_1_out = {{16{1'b0}}, IMM};  // Bit_Extender bit_extender_1
  assign bit_extender_2_out = {{16{IMM[15]}}, IMM};  // Bit_Extender bit_extender_2
  Multiplexer #(.select(2), .width(32)) multiplexer_1 (
    .in0(bit_extender_1_out), .in1(bit_extender_2_out), .in2({IMM, {16{1'b0}}}), .out(ExtIMM), .sel(ExtOp));  // open: in3, en
endmodule

module ALU (
  input  [31:0] in_1,
  input  [31:0] in_2,
  input  [2:0] ALUctr,
  output [31:0] ALUresult
);

  wire [31:0] adder_1_out, or_1_out, subtractor_1_out;

  Adder #(.width(32)) adder_1 (.a(in_1), .b(in_2), .out(adder_1_out));  // open: cin, cout
  Subtractor #(.width(32)) subtractor_1 (.a(in_1), .b(in_2), .out(subtractor_1_out));  // open: bin, bout
  assign or_1_out = in_1 | in_2;  // OR_Gate or_1, 32 bits wide
  Multiplexer #(.select(3), .width(32)) multiplexer_1 (
    .in0({32{1'b0}}), .in1(adder_1_out), .in2(subtractor_1_out), .in3(or_1_out), .in4(in_2), .out(ALUresult),
    .sel(ALUctr));  // open: in5, in6, in7, en

  // Other names for the same wires on the sheet: A[31:0] = in_1; B[31:0] = in_2
endmodule

module DM (
  input  [4:0] A,
  input  [31:0] WD,
  input  WE,
  input  Clk,
  output [31:0] RD
);

  RAM #(.addrWidth(5), .dataWidth(32), .bus("separate")) ram_1 (
    .addr(A), .din(WD), .data(RD), .str(WE), .clk(Clk));  // open: sel, ld, clr
endmodule

module NPC (
  input  [31:0] nPC1,
  input  nPC_sel2,
  input  Reset,
  input  clk,
  input  [31:0] nPC2,
  output [31:0] nPC
);

  wire [31:0] multiplexer_1_out, multiplexer_2_out;

  Multiplexer #(.width(32)) multiplexer_1 (
    .in0(nPC1), .in1(nPC2), .out(multiplexer_1_out), .sel(nPC_sel2));  // open: en
  Multiplexer #(.width(32)) multiplexer_2 (
    .in0(multiplexer_1_out), .in1({32{1'b0}}), .out(multiplexer_2_out), .sel(Reset));  // open: en
  Register #(.width(32)) PC (.D(multiplexer_2_out), .Q(nPC), .clk(clk));  // open: en, clr
endmodule
